# Fritzing sketch schema (saved by Fritzing 0.9.2b)
breadboards: 1

parts:
  Part1 = Arduino Nano (Rev3.0)
  VCC1 = Battery
  IC1 = L293D [package=THT]
  M1 = DC Motor
  M2 = Stepper Motor - Unipolar
  IR1 = TSOP312.., 314.. [package=THT]

nets:
  GND: Part1.GND, VCC1.-, IC1.0V, M2.D, IR1.GND
  N1: Part1.D2, IC1.In_1
  N2: Part1.D3, IC1.In_2
  N3: Part1.D5, IR1.Data
  N4: Part1.D8, M2.COMMON_2
  N5: Part1.D9, M2.B
  N6: Part1.D10, M2.C
  N7: Part1.D11/MOSI, M2.COMMON_1
  N8: Part1.VIN, VCC1.+, IC1.+Vmotor, M2.A
  N9: Part1.5V, IC1.Enable_1, IC1.+V, IR1.Vs
  N10: IC1.Out_1_(_Controlled_by_Enable_1_), M1.pin_2
  N11: IC1.Out_2_(_Controlled_by_Enable_1_), M1.pin_1

notes:
  upper line voltage (red) - 12V
  lower line voltage (orange) - 5V (regulated by Arduino)
  IR receiver
  DC motor for movement - runs on 12V, direction changed by the L293D
  stepper motor for steering
